# Fritzing sketch Labsheet1_01 (saved by Fritzing 0.9.5d)
breadboards: 1

parts:
  A1 = DORHEA ESP32 GPIO breakout board 30pin
  R1 = Basic Flex Resistor
  R2 = Resistor [tolerance=±5% resistance=220 package="0402 [SMD]"]
  C2 = Capacitor Polarized [package=cpol-radial-100uf-25v]
  M1 = DOIT Esp32 DevKit v1 (30 pins long, 11 pins width) [part_number=ESP32S-PIN30]  # not connected

nets:
  N1: A1.Pin_4, R1.pin_1, R2.Pin_1, C2.+
  N2: A1.Pin_14, A1.Pin_114, R1.Pin_2
  N3: A1.Pin_27, R2.Pin_0, C2.-

custom parts:
  DORHEA ESP32 GPIO breakout board 30pin: ESP32 shield 30P expansion board, supports two power supply : DC 6.5-16v and USB 5.V
  DOIT Esp32 DevKit v1 (30 pins long, 11 pins width): The DOIT Esp32 DevKit v1 is one of the development board created by DOIT to evaluate the ESP-WROOM-32 module. It is based on the ESP32 microcontroller that boasts Wifi, Bluetooth, Ethernet and Low Power support all in a single chip. (vanepp) made breadboard work, adjusted pin numbering and labels and reduced size of schematic and cleaned up pcb. This chip is 30pins long (2 x15) and 11 pins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
