# Fritzing sketch Labsheet3_02 (saved by Fritzing 0.9.5d)
breadboards: 1

parts:
  A1 = DORHEA ESP32 GPIO breakout board 30pin
  R1 = Basic Flex Resistor
  R2 = Resistor [tolerance=±5% resistance=220 package="0402 [SMD]"]
  C2 = Capacitor Polarized [package=cpol-radial-100uf-25v]
  M1 = DOIT Esp32 DevKit v1 (30 pins long, 11 pins width) [part_number=ESP32S-PIN30]  # not connected
  LCD2004-I2C1 = LCD2004-I2C
  A2 = BBAA100043
  J1 = Basic Servo
  R4 = Basic Flex Resistor
  MOD1 = SY8205 Mini 5V 5A Step-Down Buck Regulator [part_number=SY8205-MINI-REAL-VECTOR]
  R5 = Resistor [tolerance=±5% resistance=220 package="0402 [SMD]"]
  C3 = Capacitor Polarized [package=cpol-radial-100uf-25v]
  M3 = volt-ammeter [package=THT]
  M2 = volt-ammeter [package=THT]

nets:
  N1: A1.Pin_4, R1.pin_1, R2.Pin_1, C2.+
  N2: A1.Pin_5, R4.pin_1, R5.Pin_1, C3.+
  N3: A1.Pin_8, A2.pin3
  N4: A1.Pin_9, A2.pin2
  N5: A1.Pin_10, A2.pin1
  N6: A1.Pin_14, A1.Pin_114, R1.Pin_2, R4.Pin_2
  N7: A1.Pin_27, A1.Pin_53, A1.Pin_55, A1.Pin_85, A1.Pin_101, R2.Pin_0, C2.-, LCD2004-I2C1.GND, A2.pin4, M3.Meter_-, M2.-PWR, M2.Meter_-
  N8: A1.Pin_59, M2.Meter_+
  N9: A1.Pin_86, LCD2004-I2C1.VCC
  N10: A1.Pin_87, A1.Pin_123, LCD2004-I2C1.SDA
  N11: A1.Pin_88, A1.Pin_126, LCD2004-I2C1.SCL
  N12: A1.Pin_121, J1.pulse
  N13: J1.gnd, MOD1.IN-, MOD1.OUT-
  N14: J1.vcc, MOD1.OUT+
  N15: R5.Pin_0, C3.-

custom parts:
  DORHEA ESP32 GPIO breakout board 30pin: ESP32 shield 30P expansion board, supports two power supply : DC 6.5-16v and USB 5.V
  DOIT Esp32 DevKit v1 (30 pins long, 11 pins width): The DOIT Esp32 DevKit v1 is one of the development board created by DOIT to evaluate the ESP-WROOM-32 module. It is based on the ESP32 microcontroller that boasts Wifi, Bluetooth, Ethernet and Low Power support all in a single chip. (vanepp) made breadboard work, adjusted pin numbering and labels and reduced size of schematic and cleaned up pcb. This chip is 30pins long (2 x15) and 11 pins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
  LCD2004-I2C: A standard character display with 4x20 characters. Comes in many colors with LCM2004 IIC attached.
  BBAA100043: BBAA100043 traffic light module.
  SY8205 Mini 5V 5A Step-Down Buck Regulator: A compact high-current DC-DC step-down power regulator module based on the SY8205 chip. It converts 7V-30V input to a stable 5V output up to 5A. This version contains only the core power pins (IN+, IN-, OUT+, OUT-), removing the 6-channel servo power distribution headers.
  volt-ammeter: Volt-ammeter 0-100V 0-10A panel mount.
